// Digital circuit 1b_adder.dig as structural Verilog
module _1b_adder (
  input  A,
  input  B,
  input  C_in,
  output Sum,
  output C_out
);

  wire and_1_out, and_2_out, xor_1_out;

  xor xor_1 (xor_1_out, B, C_in);
  xor xor_2 (Sum, A, xor_1_out);
  and and_1 (and_1_out, A, xor_1_out);
  and and_2 (and_2_out, B, C_in);
  or or_1 (C_out, and_1_out, and_2_out);
endmodule
