// Digital circuit 8b_adder.dig as structural Verilog
module _8b_adder (
  input  C_in,
  input  [7:0] A_in,
  input  [7:0] B_in,
  output [7:0] Sum,
  output C_out
);

  wire _1b_adder_1_c_out, _1b_adder_2_c_out, _1b_adder_3_c_out, _1b_adder_4_c_out, _1b_adder_5_c_out,
       _1b_adder_6_c_out, _1b_adder_7_c_out;

  _1b_adder _1b_adder_1 (.A(A_in[0]), .B(B_in[0]), .C_in(C_in), .Sum(Sum[0]), .C_out(_1b_adder_1_c_out));
  _1b_adder _1b_adder_2 (.A(A_in[1]), .B(B_in[1]), .C_in(_1b_adder_1_c_out), .Sum(Sum[1]), .C_out(_1b_adder_2_c_out));
  _1b_adder _1b_adder_3 (.A(A_in[2]), .B(B_in[2]), .C_in(_1b_adder_2_c_out), .Sum(Sum[2]), .C_out(_1b_adder_3_c_out));
  _1b_adder _1b_adder_4 (.A(A_in[3]), .B(B_in[3]), .C_in(_1b_adder_3_c_out), .Sum(Sum[3]), .C_out(_1b_adder_4_c_out));
  _1b_adder _1b_adder_5 (.A(A_in[4]), .B(B_in[4]), .C_in(_1b_adder_4_c_out), .Sum(Sum[4]), .C_out(_1b_adder_5_c_out));
  _1b_adder _1b_adder_6 (.A(A_in[5]), .B(B_in[5]), .C_in(_1b_adder_5_c_out), .Sum(Sum[5]), .C_out(_1b_adder_6_c_out));
  _1b_adder _1b_adder_7 (.A(A_in[6]), .B(B_in[6]), .C_in(_1b_adder_6_c_out), .Sum(Sum[6]), .C_out(_1b_adder_7_c_out));
  _1b_adder _1b_adder_8 (.A(A_in[7]), .B(B_in[7]), .C_in(_1b_adder_7_c_out), .Sum(Sum[7]), .C_out(C_out));
endmodule
