// Digital circuit 8b_or.dig as structural Verilog
module _8b_or (
  input  [7:0] A,
  input  [7:0] B,
  output [7:0] Out
);

  or or_1 (Out[0], A[0], B[0]);
  or or_2 (Out[1], A[1], B[1]);
  or or_3 (Out[2], A[2], B[2]);
  or or_4 (Out[3], A[3], B[3]);
  or or_5 (Out[4], A[4], B[4]);
  or or_6 (Out[5], A[5], B[5]);
  or or_7 (Out[6], A[6], B[6]);
  or or_8 (Out[7], A[7], B[7]);
endmodule
