// Digital circuit 8b_xor_eq.dig as structural Verilog
module _8b_xor_eq (
  input  [7:0] A,
  input  [7:0] B,
  output [7:0] OUT
);

  xor xor_1 (OUT[0], A[0], B[0]);
  xor xor_2 (OUT[1], A[1], B[1]);
  xor xor_3 (OUT[2], A[2], B[2]);
  xor xor_4 (OUT[3], A[3], B[3]);
  xor xor_5 (OUT[4], A[4], B[4]);
  xor xor_6 (OUT[5], A[5], B[5]);
  xor xor_7 (OUT[6], A[6], B[6]);
  xor xor_8 (OUT[7], A[7], B[7]);
endmodule
