// Digital circuit alu.dig as structural Verilog
module alu (
  input  [7:0] TMP_B,
  input  [7:0] DBUS_A,
  input  [3:0] ALUop,
  input  C_in,
  output [7:0] ACC,
  output C_out,
  output ZERO
);

  wire _8b_adder_1_c_out, _8b_shl_1_c_out, _8b_shr_1_c_out, multiplexer_1_out, or_1_out, or_2_out, or_3_out;
  wire [7:0] _8b_adder_1_sum, _8b_and_1_out, _8b_or_1_out, _8b_shl_1_out, _8b_shr_1_out, _8b_xor_eq_1_out,
       multiplexer_2_out, not_1_out, not_2_out;

  assign not_1_out = ~TMP_B;  // Not not_1, 8 bits wide
  Multiplexer #(.Selector_Bits(2)) multiplexer_1 (
    .sel({ALUop[1], ALUop[2]}), .in_0(C_in), .in_1(1'b1), .in_2(1'b1), .in_3(1'b0), .out(multiplexer_1_out));
  Multiplexer #(.Selector_Bits(2), .Bits(8)) multiplexer_2 (
    .sel({ALUop[1], ALUop[2]}), .in_0(TMP_B), .in_1(not_1_out), .in_2({8{1'b0}}), .in_3({8{1'b1}}),
    .out(multiplexer_2_out));
  _8b_shl _8b_shl_1 (.A(DBUS_A), .C_out(_8b_shl_1_c_out), .Out(_8b_shl_1_out));
  _8b_shr _8b_shr_1 (.A(DBUS_A), .C_out(_8b_shr_1_c_out), .Out(_8b_shr_1_out));
  assign not_2_out = ~DBUS_A;  // Not not_2, 8 bits wide
  _8b_or _8b_or_1 (.A(DBUS_A), .B(TMP_B), .Out(_8b_or_1_out));
  _8b_and _8b_and_1 (.A(DBUS_A), .B(TMP_B), .Out(_8b_and_1_out));
  _8b_xor_eq _8b_xor_eq_1 (.A(DBUS_A), .B(TMP_B), .OUT(_8b_xor_eq_1_out));
  _8b_adder _8b_adder_1 (
    .C_in(multiplexer_1_out), .A_in(multiplexer_2_out), .B_in(DBUS_A), .Sum(_8b_adder_1_sum),
    .C_out(_8b_adder_1_c_out));
  Multiplexer #(.Selector_Bits(4)) multiplexer_3 (
    .sel(ALUop), .in_0(_8b_shl_1_c_out), .in_1(_8b_shr_1_c_out), .in_2(1'b0), .in_3(1'b0),
    .in_4(_8b_adder_1_c_out), .in_5(_8b_adder_1_c_out), .in_6(1'b0), .in_7(1'b0), .in_8(_8b_adder_1_c_out),
    .in_9(1'b0), .in_10(1'b0), .in_11(1'b0), .in_12(1'b0), .in_13(1'b0), .in_14(1'b0), .in_15(1'b0),
    .out(C_out));
  Multiplexer #(.Selector_Bits(4), .Bits(8)) multiplexer_4 (
    .sel(ALUop), .in_0(_8b_shl_1_out), .in_1(_8b_shr_1_out), .in_2(not_2_out), .in_3(_8b_adder_1_sum),
    .in_4(_8b_adder_1_sum), .in_5(_8b_adder_1_sum), .in_6({8{1'b0}}), .in_7(_8b_adder_1_sum),
    .in_8(_8b_adder_1_sum), .in_9(_8b_or_1_out), .in_10(_8b_and_1_out), .in_11(_8b_xor_eq_1_out),
    .in_12({8{1'b0}}), .in_13({8{1'b0}}), .in_14({8{1'b0}}), .in_15({8{1'b0}}), .out(ACC));
  or or_1 (or_1_out, ACC[0], ACC[1], ACC[2], ACC[3]);
  or or_2 (or_2_out, ACC[4], ACC[5], ACC[6], ACC[7]);
  or or_3 (or_3_out, or_1_out, or_2_out);
  not not_3 (ZERO, or_3_out);

  // Other names for the same wires on the sheet: CODE[3:0] = ALUop

  // Notes on the sheet:
  //   ALUop: operation code for the ALU
  //   MSB 1 = op code block '10', bits 0,1 used for alu code
  //   1000 ADD
  //   1001 OR
  //   1010 AND
  //   1011 XOR
  //   MSB 0 = op code block '00', bits 0,1,2 used for alu code
  //   0000 SHL
  //   0001 SHR
  //   0010 NOT
  //   0011 INC
  //   ---
  //   0100  CMP
  //   0101 SUB
  //   0111 DEC
  //   C_out: carry flag out
  //   C_in: carry in
endmodule
