// Digital circuit alu_flag_reg.dig as structural Verilog
module alu_flag_reg (
  input  WE_Z,
  input  [1:0] WE_C,
  input  Z_in,
  input  C_in,
  input  CLK,
  output C_out,
  output Z_out
);

  wire multiplexer_1_out, multiplexer_2_out, reset_1_out;

  Multiplexer #(.Selector_Bits(2)) multiplexer_1 (
    .sel(WE_C), .in_0(C_out), .in_1(C_in), .in_2(1'b0), .in_3(1'b1), .out(multiplexer_1_out));
  Multiplexer multiplexer_2 (.sel(WE_Z), .in_0(Z_out), .in_1(Z_in), .out(multiplexer_2_out));
  Reset #(.invertOutput("false")) reset_1 (.out(reset_1_out));
  dsc_flip_flop dsc_flip_flop_1 (
    .D(multiplexer_1_out), .CLK(CLK), .SET(1'b0), .CLR(reset_1_out), .Q(C_out));  // open: nQ
  dsc_flip_flop dsc_flip_flop_2 (
    .D(multiplexer_2_out), .CLK(CLK), .SET(1'b0), .CLR(reset_1_out), .Q(Z_out));  // open: nQ

  // Notes on the sheet:
  //   WE_C: write enable for carry flag.
  //   00 off - no write (loopback)
  //   01 write from input (from ALU)
  //   10 clear (set 0)
  //   11 set 1
endmodule
