// Digital circuit alu_full.dig as structural Verilog
module alu_full (
  input  [7:0] DBUS,
  input  CLK,
  input  [3:0] ALUop,
  input  FLGSzero_WE,
  input  [1:0] FLGScarry_WE,
  input  TMP_WE,
  input  ACC_WE,
  input  ALU_OE,
  output CARRY,
  output ZERO
);

  wire ALU_c_out, ALU_zero;
  wire [7:0] ALU_acc, REG_TMP_d_out;

  register #(.generic("dffpName := \"regACC\";")) REG_ACC (
    .WE(ACC_WE), .D_IN(ALU_acc), .OE(ALU_OE), .CLK(CLK), .D_out(DBUS));
  alu ALU (
    .DBUS_A(DBUS), .TMP_B(REG_TMP_d_out), .C_in(CARRY), .ALUop(ALUop), .C_out(ALU_c_out), .ACC(ALU_acc),
    .ZERO(ALU_zero));
  register #(.generic("dffpName := \"regTMP\";")) REG_TMP (
    .WE(TMP_WE), .D_IN(DBUS), .OE(1'b1), .CLK(CLK), .D_out(REG_TMP_d_out));
  alu_flag_reg REG_FLAG (
    .WE_Z(FLGSzero_WE), .WE_C(FLGScarry_WE), .Z_in(ALU_zero), .C_in(ALU_c_out), .CLK(CLK), .C_out(CARRY),
    .Z_out(ZERO));

  // Other names for the same wires on the sheet: ACC_OE = ALU_OE
endmodule
