// Digital circuit control_unit.dig as structural Verilog
module control_unit (
  input  CLK,
  input  [7:0] DBUS,
  input  ZERO,
  input  CARRY,
  output TMP_WE,
  output [7:0] PC_out,
  output ADDR_sel,
  output R0_OE,
  output R0_WE,
  output R1_OE,
  output R1_WE,
  output R2_OE,
  output R2_WE,
  output R3_OE,
  output R3_WE,
  output ACC_WE,
  output ACC_OE,
  output FLAG__WE_Z,
  output [1:0] FLAG__WE_C,
  output RAM_OE,
  output RAM_WE,
  output MAR_WE,
  output [3:0] ALUop
);

  wire and_1_out, and_2_out, and_3_out, and_4_out, and_5_out, and_6_out, and_7_out, and_8_out, and_9_out,
       and_10_out, and_11_out, and_12_out, and_13_out, and_14_out, and_15_out, and_18_out, and_19_out,
       and_20_out, and_21_out, and_22_out, and_25_out, and_26_out, and_27_out, and_28_out, and_29_out,
       and_30_out, and_33_out, and_34_out, and_41_out, and_42_out, and_46_out, and_47_out, BRANCH__TAKEN,
       decoder_1_out_0, decoder_1_out_1, decoder_1_out_2, decoder_1_out_3, decoder_2_out_0, decoder_2_out_1,
       decoder_2_out_2, decoder_2_out_3, decoder_3_out_0, decoder_3_out_1, decoder_3_out_2, decoder_3_out_3,
       decoder_4_out_0, decoder_4_out_2, decoder_5_out_6, decoder_6_out_0, decoder_6_out_1, decoder_6_out_2,
       decoder_6_out_3, decoder_6_out_4, decoder_6_out_5, decoder_6_out_6, decoder_6_out_7, decoder_7_out_0,
       decoder_7_out_1, decoder_7_out_2, decoder_7_out_3, FETCH, HALT, INSTR__HOUSEKEEPING, INSTR__JUMP,
       not_3_out, not_4_out, not_5_out, not_6_out, not_7_out, not_8_out, not_9_out, or_4_out, or_15_out,
       or_16_out, or_17_out, or_18_out, PC_WE, RA_OE, RA_WE, RB_OE, RB_WE, reset_1_out, T0, T1, T2, T3, T4,
       T5, T__RESET__MCR, T__RESET__NOP;
  wire [1:0] IR_d_out, IR_d_out_2, MICROCODE_ROM_d, TS;
  wire [1:1] or_19_out;
  wire [2:0] and_16_out, counter_1_out, MICROCODE_ROM_d_3;
  wire [3:0] IR_d_out_3, pulldown_1_out, pulldown_2_out;
  wire [4:3] IR_d_out_4;
  wire [7:2] MICROCODE_ROM_d_2;

  and and_1 (and_1_out, and_25_out, decoder_1_out_0);
  or or_1 (R0_OE, and_1_out, and_2_out);
  and and_2 (and_2_out, RB_OE, decoder_2_out_0);
  or or_2 (R0_WE, and_3_out, and_4_out);
  and and_3 (and_3_out, decoder_2_out_0, RB_WE);
  and and_4 (and_4_out, decoder_1_out_0, RA_WE);
  or or_3 (R1_OE, and_5_out, and_7_out);
  and and_5 (and_5_out, and_25_out, decoder_1_out_1);
  and and_6 (and_6_out, PC_WE, INSTR__JUMP, BRANCH__TAKEN);
  and and_7 (and_7_out, RB_OE, decoder_2_out_1);
  or or_4 (or_4_out, T1, PC_WE);
  or or_5 (R1_WE, and_9_out, and_8_out);
  and and_8 (and_8_out, decoder_1_out_1, RA_WE);
  and and_9 (and_9_out, decoder_2_out_1, RB_WE);
  and and_10 (and_10_out, and_25_out, decoder_1_out_2);
  program_counter PC (.WE(or_4_out), .CLK(CLK), .DBUS(DBUS), .JUMPSEL(and_6_out), .RST(1'b0), .PC_out(PC_out));
  or or_6 (R2_OE, and_10_out, and_11_out);
  and and_11 (and_11_out, RB_OE, decoder_2_out_2);
  PullDown #(.Bits(4)) pulldown_1 (.out(pulldown_1_out));
  assign ALUop = pulldown_2_out | pulldown_1_out;  // Or or_7, 4 bits wide
  PullDown #(.Bits(4)) pulldown_2 (.out(pulldown_2_out));
  or or_8 (FLAG__WE_C[0], and_21_out, FLAG__WE_Z);
  or or_9 (FLAG__WE_C[1], and_22_out, and_21_out);
  or or_10 (R2_WE, and_12_out, and_13_out);
  and and_12 (and_12_out, decoder_2_out_2, RB_WE);
  assign pulldown_1_out = decoder_4_out_0 ? {1'b0, and_16_out} : 4'bz;  // Driver driver_1
  assign pulldown_2_out = decoder_4_out_2 ? IR_d_out_3 : 4'bz;  // Driver driver_2
  and and_13 (and_13_out, decoder_1_out_2, RA_WE);
  or or_11 (R3_OE, and_14_out, and_15_out);
  and and_14 (and_14_out, and_25_out, decoder_1_out_3);
  not not_1 (IR_d_out_3[2], IR_d_out_3[3]);
  and and_15 (and_15_out, RB_OE, decoder_2_out_3);
  and and_16 (and_16_out[2], IR_d_out_3[0], IR_d_out_2[0]);
  or or_12 (and_16_out[1], and_20_out, IR_d_out_3[0]);
  or or_13 (and_16_out[0], IR_d_out_3[0], ~IR_d_out_2[0]);  // Or
  and and_17 (IR_d_out_3[1], IR_d_out_4[3], IR_d_out_3[3]);
  or or_14 (R3_WE, and_19_out, and_18_out);
  and and_18 (and_18_out, decoder_1_out_3, RA_WE);
  and and_19 (and_19_out, decoder_2_out_3, RB_WE);
  and and_20 (and_20_out, IR_d_out_2[1], IR_d_out_2[0]);
  not not_2 (INSTR__HOUSEKEEPING, or_15_out);
  and and_21 (and_21_out, decoder_3_out_3, INSTR__HOUSEKEEPING);
  and and_22 (and_22_out, INSTR__HOUSEKEEPING, decoder_3_out_2);
  and and_23 (T__RESET__NOP, INSTR__HOUSEKEEPING, decoder_3_out_1);
  and and_24 (HALT, decoder_3_out_0, INSTR__HOUSEKEEPING);
  Decoder #(.Selector_Bits(2)) decoder_1 (
    .sel(IR_d_out_2), .out_0(decoder_1_out_0), .out_1(decoder_1_out_1), .out_2(decoder_1_out_2),
    .out_3(decoder_1_out_3));
  Decoder #(.Selector_Bits(2)) decoder_2 (
    .sel(IR_d_out), .out_0(decoder_2_out_0), .out_1(decoder_2_out_1), .out_2(decoder_2_out_2),
    .out_3(decoder_2_out_3));
  or or_15 (or_15_out, or_17_out, or_16_out);
  Decoder #(.Selector_Bits(2)) decoder_3 (
    .sel(IR_d_out), .out_0(decoder_3_out_0), .out_1(decoder_3_out_1), .out_2(decoder_3_out_2),
    .out_3(decoder_3_out_3));
  or or_16 (or_16_out, IR_d_out_3[0], IR_d_out_4[3], IR_d_out_4[4], IR_d_out_3[3]);
  or or_17 (or_17_out, IR_d_out_2[0], IR_d_out_2[1]);
  register #(.generic("dffpName := \"regIR\";")) IR (
    .WE(T0), .D_IN(DBUS), .OE(1'b1), .CLK(CLK),
    .D_out({IR_d_out_3[3], IR_d_out_4, IR_d_out_3[0], IR_d_out_2, IR_d_out}));
  and and_25 (and_25_out, RA_OE, ~PC_WE);  // And
  or or_18 (or_18_out, T__RESET__NOP, T__RESET__MCR, decoder_5_out_6);
  Reset reset_1 (.out(reset_1_out));
  PriorityEncoder #(.Selector_Bits(2)) priorityencoder_1 (
    .in0(T2), .in1(T3), .in2(T4), .in3(T5), .num(TS));  // open: any
  Counter #(.Bits(3)) counter_1 (.en(reset_1_out), .C(CLK), .clr(or_18_out), .out(counter_1_out));  // open: ovf
  and and_26 (and_26_out, not_6_out, not_5_out);
  not not_3 (not_3_out, ZERO);
  not not_4 (not_4_out, CARRY);
  not not_5 (not_5_out, IR_d_out[0]);
  not not_6 (not_6_out, IR_d_out[1]);
  Decoder #(.Selector_Bits(2)) decoder_4 (
    .sel({or_19_out[1], IR_d_out_4[4]}), .out_0(decoder_4_out_0), .out_1(INSTR__JUMP), .out_2(decoder_4_out_2));  // open: out_3
  or or_19 (or_19_out[1], IR_d_out_3[3], and_28_out);
  not not_7 (not_7_out, IR_d_out_4[4]);
  Decoder #(.Selector_Bits(3)) decoder_5 (
    .sel(counter_1_out), .out_0(T0), .out_1(T1), .out_2(T2), .out_3(T3), .out_4(T4), .out_5(T5),
    .out_6(decoder_5_out_6));  // open: out_7
  or or_20 (FETCH, T0, T1);
  and and_27 (and_27_out, not_6_out, ZERO);
  and and_28 (and_28_out, not_7_out, IR_d_out_4[3]);
  // Probe TS on counter_1_out
  or or_21 (BRANCH__TAKEN, and_26_out, and_27_out, and_29_out, and_30_out);
  and and_29 (and_29_out, IR_d_out[1], IR_d_out[0], CARRY, not_3_out);
  and and_30 (and_30_out, not_5_out, not_4_out);
  and and_31 (RA_WE, decoder_6_out_0, and_47_out);
  and and_32 (RB_WE, decoder_6_out_1, and_47_out);
  or or_22 (FLAG__WE_Z, and_33_out, and_34_out);
  and and_33 (and_33_out, ACC_WE, and_42_out);
  and and_34 (and_34_out, decoder_6_out_3, and_47_out);
  and and_35 (ACC_WE, decoder_6_out_2, and_47_out);
  and and_36 (TMP_WE, decoder_6_out_4, and_47_out);
  not not_8 (not_8_out, T__RESET__MCR);
  and and_37 (PC_WE, decoder_6_out_5, and_47_out);
  Decoder #(.Selector_Bits(3)) decoder_6 (
    .sel(MICROCODE_ROM_d_3), .out_0(decoder_6_out_0), .out_1(decoder_6_out_1), .out_2(decoder_6_out_2),
    .out_3(decoder_6_out_3), .out_4(decoder_6_out_4), .out_5(decoder_6_out_5), .out_6(decoder_6_out_6),
    .out_7(decoder_6_out_7));
  and and_38 (T__RESET__MCR, MICROCODE_ROM_d_2[6], ~INSTR__HOUSEKEEPING, ~FETCH);  // And
  and and_39 (MAR_WE, decoder_6_out_6, and_47_out);
  and and_40 (RAM_WE, decoder_6_out_7, and_47_out);
  and and_41 (and_41_out, MICROCODE_ROM_d_2[7], not_8_out);
  and and_42 (and_42_out, and_47_out, MICROCODE_ROM_d_2[2]);
  and and_43 (RA_OE, decoder_7_out_0, and_47_out);
  ROM #(.AddrBits(6), .Bits(8)) MICROCODE_ROM (
    .A({IR_d_out_3[3], IR_d_out_4, IR_d_out_3[0], TS}), .sel(1'b1),
    .D({MICROCODE_ROM_d_2[7:6], MICROCODE_ROM_d_3, MICROCODE_ROM_d_2[2], MICROCODE_ROM_d}));
  and and_44 (RB_OE, decoder_7_out_1, and_47_out);
  and and_45 (ACC_OE, decoder_7_out_2, and_47_out);
  Decoder #(.Selector_Bits(2)) decoder_7 (
    .sel(MICROCODE_ROM_d), .out_0(decoder_7_out_0), .out_1(decoder_7_out_1), .out_2(decoder_7_out_2),
    .out_3(decoder_7_out_3));
  and and_46 (and_46_out, decoder_7_out_3, and_47_out);
  not not_9 (not_9_out, T0);
  or or_23 (RAM_OE, T0, and_46_out);
  Multiplexer multiplexer_1 (.sel(not_9_out), .in_0(1'b0), .in_1(and_42_out), .out(ADDR_sel));
  and and_47 (and_47_out, and_41_out, ~INSTR__HOUSEKEEPING, ~FETCH);  // And

  // Other names for the same wires on the sheet: FLGS_WE = FLAG__WE_Z

  // Notes on the sheet:
  //   FLAG__WE_C: write enable for carry flag.
  //   00 off - no write (loopback)
  //   01 write from input (from ALU)
  //   10 clear (set 0)
  //   11 set 1
  //   PROGRAM COUNTER MANAGEMENT
  //   ALU OP MAPPING
  //   00 region
  //   1reg ALUop +
  //   CMP & SUB
  //   10 region
  //   2reg ALUop
  //   SEC
  //   CLC
  //   NOP
  //   HALT
  //   RA
  //   RB
  //   TIME STATE HANDLER
  //   H G F E D C B A
  //   BRANCH TAKEN
  //   INSTR TYPE
  //   00: ALU single reg
  //   01: JUMP type 
  //   10: ALU double reg
  //   11: MEM type (unused)
  //   000
  //   RA
  //   001
  //   RB
  //   ROM ACTIVE MASK
  //   011
  //   FLGS
  //   010
  //   ACC
  //   100
  //   TMP
  //   101
  //   PC
  //   DST
  //   111
  //   RAM
  //   110
  //   MAR
  //   ADDRSEL
  //   &
  //   enFLGS
  //   00
  //   RA
  //   MICROCODE_ROM loads microcoderom.hex
  //   01
  //   RB
  //   10
  //   ACC
  //   SRC
  //   11
  //   RAM
  //   contents of MICROCODE ROM (hex, n*v repeats v):
  //   /home/alper/Documents/alp-computer/microcoderom.hex false
endmodule
