// Digital circuit cu_tstate_counter.dig as structural Verilog
module cu_tstate_counter (
  input  CLK,
  input  RST,
  output T0,
  output T1,
  output T2,
  output T3,
  output T4,
  output T5
);

  wire nor_1_out, or_1_out, reset_1_out;

  nor nor_1 (nor_1_out, T0, T1, T2, T3, T4);
  or or_1 (or_1_out, RST, reset_1_out);
  Reset #(.invertOutput("false")) reset_1 (.out(reset_1_out));
  dsc_flip_flop dsc_flip_flop_1 (.D(nor_1_out), .CLK(CLK), .SET(1'b0), .CLR(or_1_out), .Q(T0));  // open: nQ
  dsc_flip_flop dsc_flip_flop_2 (.D(T0), .CLK(CLK), .SET(1'b0), .CLR(or_1_out), .Q(T1));  // open: nQ
  dsc_flip_flop dsc_flip_flop_3 (.D(T1), .CLK(CLK), .SET(1'b0), .CLR(or_1_out), .Q(T2));  // open: nQ
  dsc_flip_flop dsc_flip_flop_4 (.D(T2), .CLK(CLK), .SET(1'b0), .CLR(or_1_out), .Q(T3));  // open: nQ
  dsc_flip_flop dsc_flip_flop_5 (.D(T3), .CLK(CLK), .SET(1'b0), .CLR(or_1_out), .Q(T4));  // open: nQ
  dsc_flip_flop dsc_flip_flop_6 (.D(T4), .CLK(CLK), .SET(1'b0), .CLR(or_1_out), .Q(T5));  // open: nQ
endmodule
