// Digital circuit program_counter.dig as structural Verilog
module program_counter (
  input  WE,
  input  CLK,
  input  [7:0] DBUS,
  input  JUMPSEL,
  input  RST,
  output [7:0] PC_out
);

  wire _1b_half_adder_1_c, _1b_half_adder_2_c, _1b_half_adder_3_c, _1b_half_adder_4_c, _1b_half_adder_5_c,
       _1b_half_adder_6_c, _1b_half_adder_7_c, or_1_out, reset_1_out;
  wire [7:0] _1b_half_adder_1_s, multiplexer_1_out, multiplexer_2_out;

  Multiplexer #(.Bits(8)) multiplexer_1 (
    .sel(JUMPSEL), .in_0(_1b_half_adder_1_s), .in_1(DBUS), .out(multiplexer_1_out));
  Reset #(.invertOutput("false")) reset_1 (.out(reset_1_out));
  or or_1 (or_1_out, RST, reset_1_out);
  Multiplexer #(.Bits(8)) multiplexer_2 (.sel(WE), .in_0(PC_out), .in_1(multiplexer_1_out), .out(multiplexer_2_out));
  dsc_flip_flop dsc_flip_flop_1 (
    .D(multiplexer_2_out[0]), .CLK(CLK), .SET(1'b0), .CLR(or_1_out), .Q(PC_out[0]));  // open: nQ
  dsc_flip_flop dsc_flip_flop_2 (
    .D(multiplexer_2_out[1]), .CLK(CLK), .SET(1'b0), .CLR(or_1_out), .Q(PC_out[1]));  // open: nQ
  dsc_flip_flop dsc_flip_flop_3 (
    .D(multiplexer_2_out[2]), .CLK(CLK), .SET(1'b0), .CLR(or_1_out), .Q(PC_out[2]));  // open: nQ
  dsc_flip_flop dsc_flip_flop_4 (
    .D(multiplexer_2_out[3]), .CLK(CLK), .SET(1'b0), .CLR(or_1_out), .Q(PC_out[3]));  // open: nQ
  dsc_flip_flop dsc_flip_flop_5 (
    .D(multiplexer_2_out[4]), .CLK(CLK), .SET(1'b0), .CLR(or_1_out), .Q(PC_out[4]));  // open: nQ
  dsc_flip_flop dsc_flip_flop_6 (
    .D(multiplexer_2_out[5]), .CLK(CLK), .SET(1'b0), .CLR(or_1_out), .Q(PC_out[5]));  // open: nQ
  dsc_flip_flop dsc_flip_flop_7 (
    .D(multiplexer_2_out[6]), .CLK(CLK), .SET(1'b0), .CLR(or_1_out), .Q(PC_out[6]));  // open: nQ
  dsc_flip_flop dsc_flip_flop_8 (
    .D(multiplexer_2_out[7]), .CLK(CLK), .SET(1'b0), .CLR(or_1_out), .Q(PC_out[7]));  // open: nQ
  // Probe regPC on PC_out
  _1b_half_adder _1b_half_adder_1 (.A(1'b1), .B(PC_out[0]), .S(_1b_half_adder_1_s[0]), .C(_1b_half_adder_1_c));
  _1b_half_adder _1b_half_adder_2 (
    .A(_1b_half_adder_1_c), .B(PC_out[1]), .S(_1b_half_adder_1_s[1]), .C(_1b_half_adder_2_c));
  _1b_half_adder _1b_half_adder_3 (
    .A(_1b_half_adder_2_c), .B(PC_out[2]), .S(_1b_half_adder_1_s[2]), .C(_1b_half_adder_3_c));
  _1b_half_adder _1b_half_adder_4 (
    .A(_1b_half_adder_3_c), .B(PC_out[3]), .S(_1b_half_adder_1_s[3]), .C(_1b_half_adder_4_c));
  _1b_half_adder _1b_half_adder_5 (
    .A(_1b_half_adder_4_c), .B(PC_out[4]), .S(_1b_half_adder_1_s[4]), .C(_1b_half_adder_5_c));
  _1b_half_adder _1b_half_adder_6 (
    .A(_1b_half_adder_5_c), .B(PC_out[5]), .S(_1b_half_adder_1_s[5]), .C(_1b_half_adder_6_c));
  _1b_half_adder _1b_half_adder_7 (
    .A(_1b_half_adder_6_c), .B(PC_out[6]), .S(_1b_half_adder_1_s[6]), .C(_1b_half_adder_7_c));
  _1b_half_adder _1b_half_adder_8 (.A(_1b_half_adder_7_c), .B(PC_out[7]), .S(_1b_half_adder_1_s[7]));  // open: C

  // Notes on the sheet:
  //   JUMPSEL: read the data from the bus rather than the internal incrementer.
  //   RST: reset
endmodule
