// Digital circuit cpu.dig as structural Verilog
module cpu (
  input  CLK
);

  wire alu_full_1_carry, alu_full_1_zero, and_1_out, control_unit_1_acc_oe, control_unit_1_acc_we,
       control_unit_1_addr_sel, control_unit_1_flag__we_z, control_unit_1_mar_we, control_unit_1_r0_oe,
       control_unit_1_r0_we, control_unit_1_r1_oe, control_unit_1_r1_we, control_unit_1_r2_oe,
       control_unit_1_r2_we, control_unit_1_r3_oe, control_unit_1_r3_we, control_unit_1_ram_oe,
       control_unit_1_ram_we, control_unit_1_tmp_we;
  wire [1:0] control_unit_1_flag__we_c;
  wire [3:0] control_unit_1_aluop;
  wire [7:0] control_unit_1_pc_out, MAR_d_out, multiplexer_1_out, REG_0__A_d_out;

  alu_full alu_full_1 (
    .DBUS(REG_0__A_d_out), .CLK(CLK), .ALU_OE(control_unit_1_acc_oe), .ACC_WE(control_unit_1_acc_we),
    .TMP_WE(control_unit_1_tmp_we), .ZERO(alu_full_1_zero), .CARRY(alu_full_1_carry),
    .ALUop(control_unit_1_aluop), .FLGSzero_WE(control_unit_1_flag__we_z),
    .FLGScarry_WE(control_unit_1_flag__we_c));
  register #(.generic("dffpName := \"reg0A\";")) REG_0__A (
    .WE(control_unit_1_r0_we), .D_IN(REG_0__A_d_out), .OE(control_unit_1_r0_oe), .CLK(CLK),
    .D_out(REG_0__A_d_out));
  control_unit control_unit_1 (
    .DBUS(REG_0__A_d_out), .ACC_OE(control_unit_1_acc_oe), .ACC_WE(control_unit_1_acc_we),
    .TMP_WE(control_unit_1_tmp_we), .ZERO(alu_full_1_zero), .CARRY(alu_full_1_carry),
    .ALUop(control_unit_1_aluop), .FLAG__WE_Z(control_unit_1_flag__we_z),
    .FLAG__WE_C(control_unit_1_flag__we_c), .PC_out(control_unit_1_pc_out),
    .ADDR_sel(control_unit_1_addr_sel), .MAR_WE(control_unit_1_mar_we), .RAM_WE(control_unit_1_ram_we),
    .RAM_OE(control_unit_1_ram_oe), .CLK(CLK), .R0_OE(control_unit_1_r0_oe), .R0_WE(control_unit_1_r0_we),
    .R1_OE(control_unit_1_r1_oe), .R1_WE(control_unit_1_r1_we), .R2_OE(control_unit_1_r2_oe),
    .R2_WE(control_unit_1_r2_we), .R3_OE(control_unit_1_r3_oe), .R3_WE(control_unit_1_r3_we));
  register #(.generic("dffpName := \"reg1B\";")) REG_1__B (
    .WE(control_unit_1_r1_we), .D_IN(REG_0__A_d_out), .OE(control_unit_1_r1_oe), .CLK(CLK),
    .D_out(REG_0__A_d_out));
  register #(.generic("dffpName := \"reg2C\";")) REG_2__C (
    .WE(control_unit_1_r2_we), .D_IN(REG_0__A_d_out), .OE(control_unit_1_r2_oe), .CLK(CLK),
    .D_out(REG_0__A_d_out));
  register #(.generic("dffpName := \"reg3D\";")) REG_3__D (
    .WE(control_unit_1_r3_we), .D_IN(REG_0__A_d_out), .OE(control_unit_1_r3_oe), .CLK(CLK),
    .D_out(REG_0__A_d_out));
  register #(.generic("dffpName := \"regMAR\";")) MAR (
    .WE(control_unit_1_mar_we), .D_IN(REG_0__A_d_out), .OE(1'b1), .CLK(CLK), .D_out(MAR_d_out));
  Multiplexer #(.Bits(8)) multiplexer_1 (
    .sel(control_unit_1_addr_sel), .in_0(control_unit_1_pc_out), .in_1(MAR_d_out), .out(multiplexer_1_out));
  and and_1 (and_1_out, CLK, control_unit_1_ram_we);
  EEPROM #(.AddrBits(8), .isProgramMemory("true"), .Bits(8)) RAM (
    .A(multiplexer_1_out), .CS(1'b1), .WE(and_1_out), .OE(control_unit_1_ram_oe), .D(REG_0__A_d_out));

  // Notes on the sheet:
  //   CLK: Hz: 10
  //   contents of RAM (hex, n*v repeats v):
  //   f8,b1,fc,b3,c2,c7,2,84,13,13,d7,16,c2,12,12,c6,84,43,19,12,12
  //   ,d6,16,40,4,b0,d3,40,1b,150*0,1,0,1,0,2,0,3,0,5,0,8,0,d,0,15,0
  //   ,22,0,37,0,59,0,90,0,e9,1,79,2,62,3,db,6,3d,a,18,10,55,1a,6d,2a
  //   ,c2,45,2f,6f,f1,b5,20
endmodule
