// Digital circuit dsc_flip_flop.dig as structural Verilog
module dsc_flip_flop (
  input  D,
  input  CLK,
  input  SET,
  input  CLR,
  output Q,
  output nQ
);

  wire nand_1_out, nand_2_out, nand_3_out, nand_4_out, nand_5_out, nand_6_out, not_1_out, not_2_out,
       not_3_out, not_4_out, not_5_out, not_6_out;

  not not_1 (not_1_out, CLK);
  not not_2 (not_2_out, D);
  nand nand_1 (nand_1_out, D, not_1_out);
  nand nand_2 (nand_2_out, not_1_out, not_2_out);
  not not_3 (not_3_out, not_1_out);
  not not_4 (not_4_out, SET);
  not not_5 (not_5_out, CLR);
  nand nand_3 (nand_3_out, nand_1_out, not_4_out, nand_4_out);
  nand nand_4 (nand_4_out, nand_3_out, not_5_out, nand_2_out);
  not not_6 (not_6_out, nand_3_out);
  nand nand_5 (nand_5_out, nand_3_out, not_3_out);
  nand nand_6 (nand_6_out, not_3_out, not_6_out);
  nand nand_7 (Q, nand_5_out, not_4_out, nQ);
  nand nand_8 (nQ, Q, not_5_out, nand_6_out);
endmodule
