// Digital circuit register.dig as structural Verilog
module register (
  input  WE,
  input  [7:0] D_IN,
  input  OE,
  input  CLK,
  output [7:0] D_out
);

  wire [7:0] dsc_flip_flop_1_q, multiplexer_1_out;

  Multiplexer #(.Bits(8)) multiplexer_1 (.sel(WE), .in_0(dsc_flip_flop_1_q), .in_1(D_IN), .out(multiplexer_1_out));
  dsc_flip_flop dsc_flip_flop_1 (
    .D(multiplexer_1_out[0]), .CLK(CLK), .SET(1'b0), .CLR(1'b0), .Q(dsc_flip_flop_1_q[0]));  // open: nQ
  dsc_flip_flop dsc_flip_flop_2 (
    .D(multiplexer_1_out[1]), .CLK(CLK), .SET(1'b0), .CLR(1'b0), .Q(dsc_flip_flop_1_q[1]));  // open: nQ
  dsc_flip_flop dsc_flip_flop_3 (
    .D(multiplexer_1_out[2]), .CLK(CLK), .SET(1'b0), .CLR(1'b0), .Q(dsc_flip_flop_1_q[2]));  // open: nQ
  dsc_flip_flop dsc_flip_flop_4 (
    .D(multiplexer_1_out[3]), .CLK(CLK), .SET(1'b0), .CLR(1'b0), .Q(dsc_flip_flop_1_q[3]));  // open: nQ
  dsc_flip_flop dsc_flip_flop_5 (
    .D(multiplexer_1_out[4]), .CLK(CLK), .SET(1'b0), .CLR(1'b0), .Q(dsc_flip_flop_1_q[4]));  // open: nQ
  dsc_flip_flop dsc_flip_flop_6 (
    .D(multiplexer_1_out[5]), .CLK(CLK), .SET(1'b0), .CLR(1'b0), .Q(dsc_flip_flop_1_q[5]));  // open: nQ
  dsc_flip_flop dsc_flip_flop_7 (
    .D(multiplexer_1_out[6]), .CLK(CLK), .SET(1'b0), .CLR(1'b0), .Q(dsc_flip_flop_1_q[6]));  // open: nQ
  dsc_flip_flop dsc_flip_flop_8 (
    .D(multiplexer_1_out[7]), .CLK(CLK), .SET(1'b0), .CLR(1'b0), .Q(dsc_flip_flop_1_q[7]));  // open: nQ
  assign D_out = OE ? dsc_flip_flop_1_q : 8'bz;  // Driver driver_1
  // Probe val on dsc_flip_flop_1_q
endmodule
